// Logisim project vending machine.circ as structural Verilog: 1 circuit, main circuit main
module main (
  input  C,
  input  D,
  output out_3
);

  wire and_1_out, and_2_out, and_3_out, and_4_out, and_5_out, and_6_out, clock_1_out, d_ff_1_q, d_ff_2_q,
       not_1_out, not_2_out, not_3_out, not_4_out, or_1_out, or_2_out;

  not not_1 (not_1_out, C);
  not not_2 (not_2_out, D);
  and and_1 (and_1_out, not_3_out, C);
  and and_2 (and_2_out, not_3_out, D, not_1_out);
  and and_3 (and_3_out, C, not_2_out, not_4_out);
  and and_4 (and_4_out, not_3_out, d_ff_2_q, D);
  and and_5 (and_5_out, not_3_out, d_ff_2_q, not_1_out);
  Clock clock_1 (.out(clock_1_out));
  or or_1 (or_1_out, and_1_out, and_6_out, and_4_out);
  or or_2 (or_2_out, and_5_out, and_2_out, and_6_out, and_3_out);
  D_Flip_Flop d_ff_1 (.clk(clock_1_out), .D(or_1_out), .Q(d_ff_1_q));  // open: Qn, preset, en, reset
  D_Flip_Flop d_ff_2 (.clk(clock_1_out), .D(or_2_out), .Q(d_ff_2_q));  // open: Qn, preset, en, reset
  not not_3 (not_3_out, d_ff_1_q);
  and and_6 (and_6_out, d_ff_1_q, not_4_out);
  not not_4 (not_4_out, d_ff_2_q);
  and and_7 (out_3, d_ff_1_q, d_ff_2_q);
endmodule
